# Fritzing sketch tube-radio-FM (saved by Fritzing 0.9.3b)

parts:
  RDA5807M_R102 = DIP - 10 pins [chip_label=IC package="DIP (Dual Inline) [THT]"]
  Composant1 = Arduino Pro Mini v13
  1K = Resistor [tolerance=±5% resistance=220 package=THT]
  1K_2 = Resistor [tolerance=±5% resistance=220 package=THT]
  NE555 = General purpose bipolar Timer [package=dil-08]
  1M = Resistor [tolerance=±5% resistance=220 package=THT]
  1M_2 = Resistor [tolerance=±5% resistance=220 package=THT]

nets:
  N1: RDA5807M_R102.DATA, Composant1.A4
  N2: RDA5807M_R102.SCLK, Composant1.A5
  VCC: RDA5807M_R102.VCC, Composant1.VCC, NE555._RES, NE555.VCC+, 1M.Pin_1
  GND: RDA5807M_R102.GND, Composant1.GND, NE555.GND
  N3: RDA5807M_R102.LOUT, 1K.Pin_1
  N4: RDA5807M_R102.ROUT, 1K_2.Pin_1
  N5: Composant1.D5_PWM, NE555.OUT
  N6: 1K.Pin_0, 1K_2.Pin_0
  N7: NE555.TRI, NE555.TRE, 1M_2.Pin_1
  N8: NE555.DIS, 1M.Pin_0, 1M_2.Pin_0

notes:
  5V
  pick up
  amp input
  Variable Capacitor
  3.3V

custom parts:
  DIP - 10 pins: A DIP stand-in part for whatever IC you want. With 10 pins on a 300mil dual inline package (DIP) footprint.
